// Logisim project alu.circ as structural Verilog: 1 circuit, main circuit alu
module alu (
  input  [31:0] A,
  input  [31:0] B,
  input  [3:0] ALUSel,
  output [31:0] Result
);

  wire [0:0] SLT;
  wire [31:0] add, AND1, BSEL, DIVU, MUL, MULHU, MULU, OR1, REMU, SLL1, SRA1, SRL1, SUB, XOR1;

  assign AND1 = A & B;  // AND_Gate and_1, 32 bits wide
  assign OR1 = A | B;  // OR_Gate or_1, 32 bits wide
  assign XOR1 = A ^ B;  // XOR_Gate xor_1, 32 bits wide
  Shifter #(.width(32), .shift("lr")) shifter_1 (.in(A), .\dist (B[4:0]), .out(SRL1));
  Shifter #(.width(32), .shift("ar")) shifter_2 (.in(A), .\dist (B[4:0]), .out(SRA1));
  Shifter #(.width(32)) shifter_3 (.in(A), .\dist (B[4:0]), .out(SLL1));
  Adder #(.width(32)) adder_1 (.a(A), .b(B), .out(add));  // open: cin, cout
  Multiplexer #(.select(4), .width(32), .enable("false")) multiplexer_1 (
    .in0(add), .in1(AND1), .in2(OR1), .in3(XOR1), .in4(SRL1), .in5(SRA1), .in6(SLL1),
    .in7({{31{1'b0}}, SLT[0]}), .in8(DIVU), .in9(REMU), .in10(MUL), .in11(MULHU), .in12(SUB), .in13(BSEL),
    .in14({32{1'b0}}), .in15({32{1'b0}}), .out(Result), .sel(ALUSel));
  Comparator #(.width(32)) comparator_1 (.a(A), .b(B), .lt(SLT[0]));  // open: gt, eq
  Divider #(.width(32)) divider_1 (.a(A), .b(B), .out(DIVU));  // open: upper, rem
  Divider #(.width(32)) divider_2 (.a(A), .b(B), .rem(REMU));  // open: out, upper
  Multiplier #(.width(32)) multiplier_1 (.a(A), .b(B), .out(MUL));  // open: cin, cout
  Multiplier #(.width(32)) multiplier_2 (.a(A), .b(B), .cout(MULU));  // open: out, cin
  Subtractor #(.width(32)) subtractor_1 (.a(A), .b(B), .out(SUB));  // open: bin, bout
  Multiplexer #(.width(32), .enable("false")) multiplexer_2 (.in0(A), .in1(B), .out(BSEL), .sel(1'b1));

  // Notes on the sheet:
  //   INPUTS to your circuit
  //   DON'T CHANGE THE LOCATIONS OF THE INPUTS AND OUTPUTS!
  //   OUTPUT from your circuit
endmodule
