// Logisim project alu.circ as structural Verilog: 1 circuit, main circuit alu
module alu (
  input  [31:0] A,
  input  [31:0] B,
  input  [3:0] ALUSel,
  output [31:0] Result
);

  wire adder_5_cout, adder_7_cout, bothneg, comparator_1_lt, or_2_out;
  wire [31:0] add, adder_4_out, adder_6_out, AND1, bit_extender_2_out, bit_extender_3_out, DIVU, MUL, MULH,
       multiplexer_3_out, multiplexer_4_out, multiplier_3_cout, multiplier_3_out, multiplier_4_cout,
       multiplier_4_out, multiplier_5_cout, MULU, negator_1_out, negator_2_out, not_1_out, not_2_out,
       not_3_out, not_4_out, not_5_out, not_6_out, OR1, REMU, SLL1, SLT, SRA1, SRL1, SUB, VADDH, XOR1;

  assign AND1 = A & B;  // AND_Gate and_1, 32 bits wide
  assign OR1 = A | B;  // OR_Gate or_1, 32 bits wide
  assign XOR1 = A ^ B;  // XOR_Gate xor_1, 32 bits wide
  Shifter #(.width(32), .shift("lr")) shifter_1 (.in(A), .\dist (B[4:0]), .out(SRL1));
  Shifter #(.width(32), .shift("ar")) shifter_2 (.in(A), .\dist (B[4:0]), .out(SRA1));
  Shifter #(.width(32)) shifter_3 (.in(A), .\dist (B[4:0]), .out(SLL1));
  Adder #(.width(32)) adder_1 (.a(A), .b(B), .out(add));  // open: cin, cout
  Adder #(.width(16)) adder_2 (.a(A[15:0]), .b(B[15:0]), .out(VADDH[15:0]));  // open: cin, cout
  Adder #(.width(16)) adder_3 (.a(A[31:16]), .b(B[31:16]), .out(VADDH[31:16]));  // open: cin, cout
  Comparator #(.width(32)) comparator_1 (.a(A), .b(B), .lt(comparator_1_lt));  // open: gt, eq
  Divider #(.width(32)) divider_1 (.a(A), .b(B), .out(DIVU));  // open: upper, rem
  Divider #(.width(32)) divider_2 (.a(A), .b(B), .rem(REMU));  // open: out, upper
  Multiplier #(.width(32)) multiplier_1 (.a(A), .b(B), .out(MUL));  // open: cin, cout
  Multiplier #(.width(32)) multiplier_2 (.a(A), .b(B), .cout(MULU));  // open: out, cin
  Subtractor #(.width(32)) subtractor_1 (.a(A), .b(B), .out(SUB));  // open: bin, bout
  assign SLT = {{31{1'b0}}, comparator_1_lt};  // Bit_Extender bit_extender_1
  Multiplexer #(.select(4), .width(32), .enable("false")) multiplexer_1 (
    .in0(add), .in1(AND1), .in2(OR1), .in3(XOR1), .in4(SRL1), .in5(SRA1), .in6(SLL1), .in7(SLT), .in8(DIVU),
    .in9(REMU), .in10(MUL), .in11(MULU), .in12(SUB), .in13(B), .in14(MULH), .in15(VADDH), .out(Result),
    .sel(ALUSel));
  assign not_1_out = ~A;  // NOT_Gate not_1, 32 bits wide
  Adder #(.width(32)) adder_4 (.a(not_2_out), .b(bit_extender_2_out), .out(adder_4_out));  // open: cin, cout
  and and_2 (bothneg, A[31], B[31]);
  or or_2 (or_2_out, A[31], B[31]);
  Multiplier #(.width(32)) multiplier_3 (
    .a(not_1_out), .b(B), .out(multiplier_3_out), .cout(multiplier_3_cout));  // open: cin
  assign not_2_out = ~multiplier_3_cout;  // NOT_Gate not_2, 32 bits wide
  assign bit_extender_2_out = {{31{adder_5_cout}}, adder_5_cout};  // Bit_Extender bit_extender_2
  Multiplexer #(.width(32), .enable("false")) multiplexer_2 (
    .in0(MULU), .in1(multiplexer_4_out), .out(MULH), .sel(or_2_out));
  assign not_3_out = ~multiplier_3_out;  // NOT_Gate not_3, 32 bits wide
  Multiplexer #(.width(32), .enable("false")) multiplexer_3 (
    .in0(adder_4_out), .in1(adder_6_out), .out(multiplexer_3_out), .sel(B[31]));
  Adder #(.width(32)) adder_5 (.a(not_3_out), .b(32'h1), .cout(adder_5_cout));  // open: out, cin
  Negator #(.width(32)) negator_1 (.in(B), .out(negator_1_out));
  Multiplexer #(.width(32), .enable("false")) multiplexer_4 (
    .in0(multiplexer_3_out), .in1(multiplier_5_cout), .out(multiplexer_4_out), .sel(bothneg));
  assign not_4_out = ~B;  // NOT_Gate not_4, 32 bits wide
  Adder #(.width(32)) adder_6 (.a(not_5_out), .b(bit_extender_3_out), .out(adder_6_out));  // open: cin, cout
  Negator #(.width(32)) negator_2 (.in(A), .out(negator_2_out));
  Multiplier #(.width(32)) multiplier_4 (
    .a(not_4_out), .b(A), .out(multiplier_4_out), .cout(multiplier_4_cout));  // open: cin
  assign not_5_out = ~multiplier_4_cout;  // NOT_Gate not_5, 32 bits wide
  assign bit_extender_3_out = {{31{adder_7_cout}}, adder_7_cout};  // Bit_Extender bit_extender_3
  Multiplier #(.width(32)) multiplier_5 (
    .a(negator_2_out), .b(negator_1_out), .cout(multiplier_5_cout));  // open: out, cin
  assign not_6_out = ~multiplier_4_out;  // NOT_Gate not_6, 32 bits wide
  Adder #(.width(32)) adder_7 (.a(not_6_out), .b(32'h1), .cout(adder_7_cout));  // open: out, cin

  // Other names for the same wires on the sheet: A0to15[15:0] = A[15:0]; A16to31[15:0] = A[31:16];
  //   B0to15[15:0] = B[15:0]; B16to31[15:0] = B[31:16]

  // Notes on the sheet:
  //   INPUTS to your circuit
  //   DON'T CHANGE THE LOCATIONS OF THE INPUTS AND OUTPUTS!
  //   OUTPUT from your circuit
endmodule
