// Logisim project cpu.circ as structural Verilog: 5 circuits, main circuit main
module main (
  input  [31:0] INSTRUCTION,
  input  CLOCK,
  output [31:0] FETCH_ADDRESS,
  output [31:0] ra,
  output [31:0] sp,
  output [31:0] t0,
  output [31:0] t1,
  output [31:0] t2,
  output [31:0] s0,
  output [31:0] s1,
  output [31:0] a0
);

  wire ASel, BrEq, BrLt, BrUn, BSel, MemRW, PCSel, RegWEn;
  wire [1:0] WBSel;
  wire [2:0] ImmSel;
  wire [3:0] ALUSel;
  wire [31:0] adder_1_out, ALU_inputA, ALU_inputB, ALU_Out, imm_Gen_Out, INSTRUCTION_pipeline, MEM_Out,
       multiplexer_1_out, multiplexer_2_out, PCplus4, PROGRAM_COUNTER_pipeline, read_Data1, read_Data2,
       Write_RegFile;

  Adder #(.width(32)) adder_1 (.a(FETCH_ADDRESS), .b(32'h4), .out(adder_1_out));  // open: cin, cout
  Multiplexer #(.width(32), .enable("false")) multiplexer_1 (
    .in0(adder_1_out), .in1(ALU_Out), .out(multiplexer_1_out), .sel(PCSel));
  Register #(.width(32)) PC (.D(multiplexer_1_out), .clk(CLOCK), .Q(FETCH_ADDRESS));  // open: en, clr
  Control_Module control_module_1 (
    .Instruction(INSTRUCTION_pipeline), .BrEq(BrEq), .BrLt(BrLt), .PCSel(PCSel), .ImmSelect(ImmSel),
    .RegWEn(RegWEn), .BrUn(BrUn), .BSel(BSel), .ASel(ASel), .ALUSel(ALUSel), .MemRW(MemRW), .WBSel(WBSel));
  Register #(.width(32)) PC_reg (.D(FETCH_ADDRESS), .clk(CLOCK), .Q(PROGRAM_COUNTER_pipeline));  // open: en, clr
  // Probe on INSTRUCTION
  Multiplexer #(.width(32), .enable("false")) multiplexer_2 (
    .in0(INSTRUCTION), .in1(32'h13), .out(multiplexer_2_out), .sel(PCSel));
  Register #(.width(32)) Inst_reg (.D(multiplexer_2_out), .clk(CLOCK), .Q(INSTRUCTION_pipeline));  // open: en, clr
  immGen immgen_1 (.Instruction(INSTRUCTION_pipeline), .immSel(ImmSel), .imm(imm_Gen_Out));
  regfile_main RegFile (
    .rs2(INSTRUCTION_pipeline[24:20]), .rd(INSTRUCTION_pipeline[11:7]), .Read_Data_1(read_Data1),
    .Read_Data_2(read_Data2), .ra(ra), .sp(sp), .t0(t0), .t1(t1), .t2(t2), .s0(s0), .s1(s1), .a0(a0),
    .rs1(INSTRUCTION_pipeline[19:15]), .Write_Data(Write_RegFile), .RegWEn(RegWEn), .clk(CLOCK));
  Branch_Comp branch_comp_1 (
    .rs1(read_Data1), .rs2(read_Data2), .sign(BrUn), .opcode(INSTRUCTION_pipeline[6:0]), .BrEq(BrEq),
    .BrLT(BrLt));
  Multiplexer #(.width(32), .enable("false")) multiplexer_3 (
    .in0(read_Data2), .in1(imm_Gen_Out), .out(ALU_inputB), .sel(BSel));
  Multiplexer #(.width(32), .enable("false")) multiplexer_4 (
    .in0(read_Data1), .in1(PROGRAM_COUNTER_pipeline), .out(ALU_inputA), .sel(ASel));
  alu Arithmetic_Logic_Unit (.A(ALU_inputA), .B(ALU_inputB), .ALUSel(ALUSel), .Result(ALU_Out));
  Adder #(.width(32)) adder_2 (.a(PROGRAM_COUNTER_pipeline), .b(32'h4), .out(PCplus4));  // open: cin, cout
  mem_main DMEM (.Address(ALU_Out), .Write_Data(read_Data2), .Write_En(MemRW), .Read_Data(MEM_Out), .clk(CLOCK));
  Multiplexer #(.select(2), .width(32), .enable("false")) multiplexer_5 (
    .in0(PCplus4), .in1(ALU_Out), .in2(MEM_Out), .out(Write_RegFile), .sel(WBSel));  // open: in3

  // Other names for the same wires on the sheet: clk = CLOCK; opcode[6:0] = INSTRUCTION_pipeline[6:0];
  //   RD[4:0] = INSTRUCTION_pipeline[11:7]; RS1[4:0] = INSTRUCTION_pipeline[19:15];
  //   RS2[4:0] = INSTRUCTION_pipeline[24:20]; PROGRAM_COUNTER[31:0] = FETCH_ADDRESS

  // Notes on the sheet:
  //   Output
  //   Inputs/Outputs from run.circ. DO NOT MOVE THESE.
  //   Inputs
  //   It is OK to move the PC, RegFile, ALU, and MEM to wherever is most convenient for you when constructing your CPU, and to delete this text
  //   Inputs/Outputs from run.circ. DO NOT MOVE THESE.
endmodule

module immGen (
  input  [31:0] Instruction,
  input  [2:0] immSel,
  output [31:0] imm
);

  wire [31:0] I_final, s_final, SB_final, UJ_final;

  // Probe on Instruction[31:20]
  // Probe on {Instruction[31:12], {12{1'b0}}}
  assign I_final = {{20{Instruction[31]}}, Instruction[31:20]};  // Bit_Extender bit_extender_1
  // Probe on s_final
  assign s_final = {{20{Instruction[31]}}, {Instruction[31:25], Instruction[11:7]}};  // Bit_Extender bit_extender_2
  assign SB_final = {{19{Instruction[31]}}, {Instruction[31], Instruction[7], Instruction[30:25], Instruction[11:8], 1'b0}};  // Bit_Extender bit_extender_3
  // Probe on SB_final
  assign UJ_final = {{11{Instruction[31]}}, {Instruction[31], Instruction[19:12], Instruction[20], Instruction[30:21], 1'b0}};  // Bit_Extender bit_extender_4
  // Probe on UJ_final
  // Probe on I_final
  Multiplexer #(.select(3), .width(32), .enable("false")) multiplexer_1 (
    .in1(I_final), .in2(s_final), .in3(SB_final), .in4({Instruction[31:12], {12{1'b0}}}), .in5(UJ_final),
    .out(imm), .sel(immSel));  // open: in0, in6, in7
  // Probe on imm

  // Other names for the same wires on the sheet: I_imm[11:0] = Instruction[31:20];
  //   U_final[31:12] = Instruction[31:12]; U_imm[19:0] = Instruction[31:12]; UJ_imm1to10[9:0] = Instruction[30:21];
  //   S_imm2[6:0] = Instruction[31:25]; SB_imm5to10[5:0] = Instruction[30:25]; UJ_imm11th = Instruction[20];
  //   UJ_imm12to19[7:0] = Instruction[19:12]; SB_imm12th = Instruction[31]; UJ_imm31st = Instruction[31];
  //   S_imm1[4:0] = Instruction[11:7]; SB_imm1to4[3:0] = Instruction[11:8]; SB_imm11th = Instruction[7];
  //   final_Imm[31:0] = imm
endmodule

module Control_Module (
  input  [31:0] Instruction,
  input  BrEq,
  input  BrLt,
  output PCSel,
  output [2:0] ImmSelect,
  output RegWEn,
  output BrUn,
  output BSel,
  output ASel,
  output [3:0] ALUSel,
  output MemRW,
  output [1:0] WBSel
);

  wire add, addi, and1, and_1_out, and_2_out, and_3_out, and_7_out, and_9_out, and_20_out, and_21_out,
       and_22_out, and_23_out, and_28_out, and_49_out, and_50_out, and_51_out, and_52_out, and_53_out,
       and_54_out, andi, beq, blt, bne, Branch_logic, Branches, comparator_9_eq, comparator_10_eq,
       comparator_11_eq, comparator_12_eq, comparator_13_eq, comparator_14_eq, comparator_15_eq,
       comparator_16_eq, comparator_17_eq, comparator_18_eq, comparator_19_eq, comparator_20_eq,
       comparator_21_eq, comparator_22_eq, comparator_23_eq, comparator_24_eq, comparator_25_eq,
       comparator_26_eq, comparator_27_eq, comparator_28_eq, comparator_29_eq, comparator_30_eq,
       comparator_31_eq, comparator_32_eq, comparator_33_eq, comparator_34_eq, comparator_35_eq,
       comparator_36_eq, comparator_37_eq, comparator_38_eq, comparator_39_eq, comparator_40_eq,
       comparator_41_eq, comparator_42_eq, comparator_43_eq, divu, I_Imm, I_Loads, I_loads_logic, Imm_logic,
       jal, JALR, JALR_logic, lb, lh, lui, lw, mul, mulh, mulhu, not_1_out, or1, or_1_out, or_2_out,
       or_3_out, or_4_out, or_5_out, or_6_out, or_7_out, ori, R, R_logic, remu, S, S_logic, sll1, slli, slt1,
       slti, srai, srl1, srli, sub, U_logic, UJ_logic, vaddh, xor1, xori;
  wire [1:0] Branch_WBSel, IL_WBSel, Imm_WBSel, JALR_WBSel, R_WBSel, U_WBSel, UJ_WBSel;
  wire [3:0] and_ALUSel, divu_ALUSel, mul_ALUSel, mulh_ALUSel, mulhu_ALUSel, or_ALUSel, remu_ALUSel,
       sll_ALUSel, slt_ALUSel, sra_ALUSel, srl_ALUSel, sub_ALUSel, vaddh_ALUSel, xor_ALUSel;

  Multiplexer #(.width(4), .enable("false")) multiplexer_1 (
    .in0(4'b0000), .in1(4'b0010), .out(or_ALUSel), .sel(or_1_out));
  or or_1 (or_1_out, or1, ori);
  Multiplexer #(.width(4), .enable("false")) multiplexer_2 (
    .in0(4'b0000), .in1(4'b0001), .out(and_ALUSel), .sel(or_2_out));
  or or_2 (or_2_out, andi, and1);
  Multiplexer #(.width(4), .enable("false")) multiplexer_3 (
    .in0(4'b0000), .in1(4'b0011), .out(xor_ALUSel), .sel(or_3_out));
  or or_3 (or_3_out, xor1, xori);
  Multiplexer #(.width(4), .enable("false")) multiplexer_4 (
    .in0(4'b0000), .in1(4'b0100), .out(srl_ALUSel), .sel(or_4_out));
  or or_4 (or_4_out, srl1, srli);
  Multiplexer #(.width(4), .enable("false")) multiplexer_5 (.in0(4'b0000), .in1(4'b0101), .out(sra_ALUSel), .sel(srai));
  Comparator #(.width(7)) comparator_1 (.a(Instruction[6:0]), .b(7'b0110011), .eq(R));  // open: gt, lt
  // Probe on R
  Comparator #(.width(7)) comparator_2 (.a(Instruction[6:0]), .b(7'b0000011), .eq(I_Loads));  // open: gt, lt
  Comparator #(.width(7)) comparator_3 (.a(Instruction[6:0]), .b(7'b0010011), .eq(I_Imm));  // open: gt, lt
  // Probe on I_Imm
  Comparator #(.width(7)) comparator_4 (.a(Instruction[6:0]), .b(7'b0100011), .eq(S));  // open: gt, lt
  Comparator #(.width(7)) comparator_5 (.a(Instruction[6:0]), .b(7'b1100011), .eq(Branches));  // open: gt, lt
  Comparator #(.width(7)) comparator_6 (.a(Instruction[6:0]), .b(7'b0110111), .eq(lui));  // open: gt, lt
  Comparator #(.width(7)) comparator_7 (.a(Instruction[6:0]), .b(7'b1101111), .eq(jal));  // open: gt, lt
  Comparator #(.width(7)) comparator_8 (.a(Instruction[6:0]), .b(7'b1100111), .eq(JALR));  // open: gt, lt
  Multiplexer #(.width(4), .enable("false")) multiplexer_6 (
    .in0(4'b0000), .in1(4'b0110), .out(sll_ALUSel), .sel(or_5_out));
  or or_5 (or_5_out, sll1, slli);
  Multiplexer #(.width(4), .enable("false")) multiplexer_7 (
    .in0(4'b0000), .in1(4'b0111), .out(slt_ALUSel), .sel(or_6_out));
  or or_6 (or_6_out, slt1, slti);
  Multiplexer #(.width(4), .enable("false")) multiplexer_8 (
    .in0(4'b0000), .in1(4'b1000), .out(divu_ALUSel), .sel(divu));
  Multiplexer #(.width(4), .enable("false")) multiplexer_9 (
    .in0(4'b0000), .in1(4'b1001), .out(remu_ALUSel), .sel(remu));
  Multiplexer #(.width(4), .enable("false")) multiplexer_10 (.in0(4'b0000), .in1(4'b1010), .out(mul_ALUSel), .sel(mul));
  Multiplexer #(.width(4), .enable("false")) multiplexer_11 (
    .in0(4'b0000), .in1(4'b1011), .out(mulhu_ALUSel), .sel(mulhu));
  Multiplexer #(.width(4), .enable("false")) multiplexer_12 (.in0(4'b0000), .in1(4'b1100), .out(sub_ALUSel), .sel(sub));
  Multiplexer #(.width(4), .enable("false")) multiplexer_13 (
    .in0(4'b0000), .in1(4'b1110), .out(mulh_ALUSel), .sel(mulh));
  Multiplexer #(.width(4), .enable("false")) multiplexer_14 (
    .in0(4'b0000), .in1(4'b1111), .out(vaddh_ALUSel), .sel(vaddh));
  and and_1 (and_1_out, R, 1'b1);
  Comparator #(.width(3)) comparator_9 (.a(Instruction[14:12]), .b(3'b000), .eq(comparator_9_eq));  // open: gt, lt
  Comparator #(.width(3)) comparator_10 (.a(Instruction[14:12]), .b(3'b001), .eq(comparator_10_eq));  // open: gt, lt
  Comparator #(.width(3)) comparator_11 (.a(Instruction[14:12]), .b(3'b010), .eq(comparator_11_eq));  // open: gt, lt
  Comparator #(.width(3)) comparator_12 (.a(Instruction[14:12]), .b(3'b011), .eq(comparator_12_eq));  // open: gt, lt
  Comparator #(.width(3)) comparator_13 (.a(Instruction[14:12]), .b(3'b100), .eq(comparator_13_eq));  // open: gt, lt
  Comparator #(.width(3)) comparator_14 (.a(Instruction[14:12]), .b(3'b101), .eq(comparator_14_eq));  // open: gt, lt
  Comparator #(.width(3)) comparator_15 (.a(Instruction[14:12]), .b(3'b110), .eq(comparator_15_eq));  // open: gt, lt
  Comparator #(.width(3)) comparator_16 (.a(Instruction[14:12]), .b(3'b111), .eq(comparator_16_eq));  // open: gt, lt
  and and_2 (and_2_out, and_1_out, comparator_9_eq);
  and and_3 (and_3_out, and_1_out, comparator_10_eq);
  and and_4 (slt1, and_1_out, comparator_11_eq);
  and and_5 (mulhu, and_1_out, comparator_12_eq);
  and and_6 (xor1, and_1_out, comparator_13_eq);
  and and_7 (and_7_out, and_1_out, comparator_14_eq);
  and and_8 (or1, and_1_out, comparator_15_eq);
  and and_9 (and_9_out, and_1_out, comparator_16_eq);
  and and_10 (add, and_2_out, comparator_17_eq);
  Comparator #(.width(7)) comparator_17 (.a(Instruction[31:25]), .b({7{1'b0}}), .eq(comparator_17_eq));  // open: gt, lt
  and and_11 (sub, and_2_out, comparator_18_eq);
  Comparator #(.width(7)) comparator_18 (
    .a(Instruction[31:25]), .b(7'b0100000), .eq(comparator_18_eq));  // open: gt, lt
  and and_12 (vaddh, and_2_out, comparator_19_eq);
  Comparator #(.width(7)) comparator_19 (
    .a(Instruction[31:25]), .b(7'b0001111), .eq(comparator_19_eq));  // open: gt, lt
  and and_13 (mul, and_2_out, comparator_20_eq);
  Comparator #(.width(7)) comparator_20 (
    .a(Instruction[31:25]), .b(7'b0000001), .eq(comparator_20_eq));  // open: gt, lt
  and and_14 (sll1, and_3_out, comparator_21_eq);
  Comparator #(.width(7)) comparator_21 (.a(Instruction[31:25]), .b({7{1'b0}}), .eq(comparator_21_eq));  // open: gt, lt
  and and_15 (mulh, and_3_out, comparator_22_eq);
  Comparator #(.width(7)) comparator_22 (
    .a(Instruction[31:25]), .b(7'b0000001), .eq(comparator_22_eq));  // open: gt, lt
  and and_16 (srl1, and_7_out, comparator_23_eq);
  Comparator #(.width(7)) comparator_23 (.a(Instruction[31:25]), .b({7{1'b0}}), .eq(comparator_23_eq));  // open: gt, lt
  and and_17 (divu, and_7_out, comparator_24_eq);
  Comparator #(.width(7)) comparator_24 (
    .a(Instruction[31:25]), .b(7'b0000001), .eq(comparator_24_eq));  // open: gt, lt
  and and_18 (and1, and_9_out, comparator_25_eq);
  Comparator #(.width(7)) comparator_25 (.a(Instruction[31:25]), .b({7{1'b0}}), .eq(comparator_25_eq));  // open: gt, lt
  and and_19 (remu, and_9_out, comparator_26_eq);
  Comparator #(.width(7)) comparator_26 (
    .a(Instruction[31:25]), .b(7'b0000001), .eq(comparator_26_eq));  // open: gt, lt
  and and_20 (and_20_out, I_Imm, 1'b1);
  and and_21 (and_21_out, Branches, 1'b1);
  and and_22 (and_22_out, I_Loads, 1'b1);
  Comparator #(.width(3)) comparator_27 (.a(Instruction[14:12]), .b(3'b000), .eq(comparator_27_eq));  // open: gt, lt
  Comparator #(.width(3)) comparator_28 (.a(Instruction[14:12]), .b(3'b001), .eq(comparator_28_eq));  // open: gt, lt
  Comparator #(.width(3)) comparator_29 (.a(Instruction[14:12]), .b(3'b010), .eq(comparator_29_eq));  // open: gt, lt
  Comparator #(.width(3)) comparator_30 (.a(Instruction[14:12]), .b(3'b100), .eq(comparator_30_eq));  // open: gt, lt
  Comparator #(.width(3)) comparator_31 (.a(Instruction[14:12]), .b(3'b101), .eq(comparator_31_eq));  // open: gt, lt
  Comparator #(.width(3)) comparator_32 (.a(Instruction[14:12]), .b(3'b110), .eq(comparator_32_eq));  // open: gt, lt
  Comparator #(.width(3)) comparator_33 (.a(Instruction[14:12]), .b(3'b111), .eq(comparator_33_eq));  // open: gt, lt
  and and_23 (and_23_out, S, 1'b1);
  and and_24 (addi, and_20_out, comparator_27_eq);
  // Probe on addi
  and and_25 (slli, and_20_out, comparator_28_eq);
  and and_26 (slti, and_20_out, comparator_29_eq);
  and and_27 (xori, and_20_out, comparator_30_eq);
  and and_28 (and_28_out, and_20_out, comparator_31_eq);
  and and_29 (ori, and_20_out, comparator_32_eq);
  and and_30 (andi, and_20_out, comparator_33_eq);
  Comparator #(.width(3)) comparator_34 (.a(Instruction[14:12]), .b(3'b010), .eq(comparator_34_eq));  // open: gt, lt
  Comparator #(.width(3)) comparator_35 (.a(Instruction[14:12]), .b(3'b000), .eq(comparator_35_eq));  // open: gt, lt
  Comparator #(.width(3)) comparator_36 (.a(Instruction[14:12]), .b(3'b100), .eq(comparator_36_eq));  // open: gt, lt
  Comparator #(.width(3)) comparator_37 (.a(Instruction[14:12]), .b(3'b110), .eq(comparator_37_eq));  // open: gt, lt
  Comparator #(.width(3)) comparator_38 (.a(Instruction[14:12]), .b(3'b001), .eq(comparator_38_eq));  // open: gt, lt
  Comparator #(.width(3)) comparator_39 (.a(Instruction[14:12]), .b(3'b000), .eq(comparator_39_eq));  // open: gt, lt
  Comparator #(.width(3)) comparator_40 (.a(Instruction[14:12]), .b(3'b001), .eq(comparator_40_eq));  // open: gt, lt
  Comparator #(.width(3)) comparator_41 (.a(Instruction[14:12]), .b(3'b010), .eq(comparator_41_eq));  // open: gt, lt
  and and_31 (MemRW, and_23_out, comparator_34_eq);
  and and_32 (beq, and_21_out, comparator_35_eq);
  and and_33 (blt, and_21_out, comparator_36_eq);
  and and_34 (BrUn, and_21_out, comparator_37_eq);
  and and_35 (bne, and_21_out, comparator_38_eq);
  and and_36 (lb, and_22_out, comparator_39_eq);
  and and_37 (lh, and_22_out, comparator_40_eq);
  and and_38 (lw, and_22_out, comparator_41_eq);
  and and_39 (srli, and_28_out, comparator_42_eq);
  Comparator #(.width(7)) comparator_42 (.a(Instruction[31:25]), .b({7{1'b0}}), .eq(comparator_42_eq));  // open: gt, lt
  and and_40 (srai, and_28_out, comparator_43_eq);
  Comparator #(.width(7)) comparator_43 (
    .a(Instruction[31:25]), .b(7'b0100000), .eq(comparator_43_eq));  // open: gt, lt
  Multiplexer #(.width(2), .enable("false")) multiplexer_15 (.in0(2'b00), .in1(2'b01), .out(R_WBSel), .sel(R_logic));
  and and_41 (S_logic, S, 1'b1);
  Multiplexer #(.width(2), .enable("false")) multiplexer_16 (
    .in0(2'b00), .in1(2'b01), .out(Branch_WBSel), .sel(or_7_out));
  or or_7 (or_7_out, and_49_out, and_50_out);
  and and_42 (U_logic, lui, 1'b1);
  Multiplexer #(.width(2), .enable("false")) multiplexer_17 (.in0(2'b00), .in1(2'b01), .out(U_WBSel), .sel(U_logic));
  and and_43 (UJ_logic, jal, 1'b1);
  Multiplexer #(.width(2), .enable("false")) multiplexer_18 (.in0(2'b00), .in1(2'b10), .out(UJ_WBSel), .sel(UJ_logic));
  and and_44 (JALR_logic, JALR, 1'b1);
  Multiplexer #(.width(2), .enable("false")) multiplexer_19 (
    .in0(2'b00), .in1(2'b10), .out(JALR_WBSel), .sel(JALR_logic));
  and and_45 (Imm_logic, I_Imm, 1'b1);
  Multiplexer #(.width(2), .enable("false")) multiplexer_20 (
    .in0(2'b00), .in1(2'b01), .out(Imm_WBSel), .sel(Imm_logic));
  and and_46 (R_logic, R, 1'b1);
  and and_47 (I_loads_logic, I_Loads, 1'b1);
  and and_48 (Branch_logic, Branches, 1'b1);
  and and_49 (and_49_out, BrLt, blt);
  and and_50 (and_50_out, BrEq, beq);
  // Probe on Imm_WBSel
  Multiplexer #(.width(2), .enable("false")) multiplexer_21 (
    .in0(2'b00), .in1(2'b10), .out(IL_WBSel), .sel(I_loads_logic));
  not not_1 (not_1_out, BrEq);
  and and_51 (and_51_out, blt, BrLt);
  and and_52 (and_52_out, BrUn, BrLt);
  and and_53 (and_53_out, not_1_out, bne);
  or or_8 (BSel, I_Imm, I_Loads, S, Branches, JALR, lui, jal);
  and and_54 (and_54_out, beq, BrEq);
  or or_9 (RegWEn, R, I_Loads, I_Imm, lui, jal, JALR);
  assign WBSel = R_WBSel | IL_WBSel | U_WBSel | JALR_WBSel | Imm_WBSel | Branch_WBSel;  // OR_Gate or_10, 2 bits wide
  // Probe on WBSel
  IMMSEL immsel_1 (.Instruction(Instruction), .ImmSel(ImmSelect));
  // Probe on ImmSelect
  or or_11 (PCSel, and_54_out, and_51_out, and_52_out, and_53_out, jal, JALR);
  or or_12 (ASel, beq, blt, BrUn, bne, jal);
  assign ALUSel = 4'b0000 | or_ALUSel | and_ALUSel | xor_ALUSel | srl_ALUSel | sra_ALUSel | sll_ALUSel | slt_ALUSel | divu_ALUSel | remu_ALUSel | mul_ALUSel | mulhu_ALUSel | sub_ALUSel | mulh_ALUSel | vaddh_ALUSel;  // OR_Gate or_13, 4 bits wide
  // Probe on ALUSel

  // Other names for the same wires on the sheet: bltu = BrUn; opcode[6:0] = Instruction[6:0];
  //   rd[4:0] = Instruction[11:7]; func3[2:0] = Instruction[14:12]; rs1[4:0] = Instruction[19:15];
  //   rs2[4:0] = Instruction[24:20]; func7[6:0] = Instruction[31:25]; UJ = jal; U = lui; sw = MemRW

  // Notes on the sheet:
  //   R-TYPE
  //   I-TYPE
  //   U-TYPE
  //   UJ-TYPE
  //   I-TYPE3
  //   I-TYPE2
  //   S-TYPE
  //   SB-TYPE
  //   ALUSel
endmodule

module Branch_Comp (
  input  [31:0] rs1,
  input  [31:0] rs2,
  input  sign,
  input  [6:0] opcode,
  output BrEq,
  output BrLT
);

  wire B, comparator_1_eq, comparator_1_lt, comparator_2_eq, comparator_2_lt, multiplexer_1_out,
       multiplexer_2_out;

  Comparator #(.width(32)) comparator_1 (.a(rs1), .b(rs2), .eq(comparator_1_eq), .lt(comparator_1_lt));  // open: gt
  Comparator #(.width(32), .mode("unsigned")) comparator_2 (
    .a(rs1), .b(rs2), .eq(comparator_2_eq), .lt(comparator_2_lt));  // open: gt
  Comparator #(.width(7)) comparator_3 (.a(opcode), .b(7'b1100011), .eq(B));  // open: gt, lt
  Multiplexer #(.enable("false")) multiplexer_1 (
    .in0(comparator_1_eq), .in1(comparator_2_eq), .out(multiplexer_1_out), .sel(sign));
  Multiplexer #(.enable("false")) multiplexer_2 (
    .in0(comparator_1_lt), .in1(comparator_2_lt), .out(multiplexer_2_out), .sel(sign));
  and and_1 (BrEq, multiplexer_1_out, B);
  and and_2 (BrLT, multiplexer_2_out, B);

  // Other names for the same wires on the sheet: reg1[31:0] = rs1; reg2[31:0] = rs2
endmodule

module IMMSEL (
  input  [31:0] Instruction,
  output [2:0] ImmSel
);

  wire comparator_2_eq, comparator_3_eq, comparator_4_eq, I, R, S, SB, U, UJ;

  Comparator #(.width(7)) comparator_1 (.a(Instruction[6:0]), .b(7'b0110011), .eq(R));  // open: gt, lt
  Comparator #(.width(7)) comparator_2 (.a(Instruction[6:0]), .b(7'b0000011), .eq(comparator_2_eq));  // open: gt, lt
  Comparator #(.width(7)) comparator_3 (.a(Instruction[6:0]), .b(7'b0010011), .eq(comparator_3_eq));  // open: gt, lt
  Comparator #(.width(7)) comparator_4 (.a(Instruction[6:0]), .b(7'b1100111), .eq(comparator_4_eq));  // open: gt, lt
  Comparator #(.width(7)) comparator_5 (.a(Instruction[6:0]), .b(7'b0100011), .eq(S));  // open: gt, lt
  Comparator #(.width(7)) comparator_6 (.a(Instruction[6:0]), .b(7'b1100011), .eq(SB));  // open: gt, lt
  Comparator #(.width(7)) comparator_7 (.a(Instruction[6:0]), .b(7'b0110111), .eq(U));  // open: gt, lt
  Comparator #(.width(7)) comparator_8 (.a(Instruction[6:0]), .b(7'b1101111), .eq(UJ));  // open: gt, lt
  or or_1 (I, comparator_2_eq, comparator_3_eq, comparator_4_eq);
  Priority_Encoder priority_encoder_1 (
    .in0(R), .in1(I), .in2(S), .in3(SB), .in4(U), .in5(UJ), .out(ImmSel));  // open: in6, in7, en_in, gs, en_out

  // Other names for the same wires on the sheet: Opcode[6:0] = Instruction[6:0]

  // Notes on the sheet:
  //   R-TYPE
  //   I-TYPE
  //   I-TYPE2
  //   S-TYPE
  //   SB-TYPE
  //   U-TYPE
  //   UJ-TYPE
  //   I-TYPE3
endmodule
